// Logisim project cpu_architecture.circ as structural Verilog: 4 circuits, main circuit main
module main (
  input  WE,
  input  [15:0] in_2,
  output HALT
);

  wire add, and0, and_1_out, and_2_out, beq, bgtz, blez, bne, button_1_out, button_2_out, clk, clock_1_out,
       div, divu, j, jal, jalr, jr, li, lw, mfhi, mflo, mthi, mtlo, mult, multu, nor0, not_1_out,
       opcodedecoder_1_aluen, opcodedecoder_1_i_type, opcodedecoder_1_j_type, opcodedecoder_1_regen, or0,
       or_1_out, por_1_out, por_2_out, shift_register_1_p4, shift_register_1_p5, shift_register_1_p6,
       shift_register_1_p7, sll0, slti, sltiu, sra0, srl0, sub, sw, xor0;
  wire [4:0] multiplexer_1_out, opcodedecoder_1_operation, opcodedecoder_1_rd, opcodedecoder_1_rs,
       opcodedecoder_1_rt, opcodedecoder_1_shamt;
  wire [15:0] alu_1_imm_out, alu_1_peek_hi, alu_1_peek_lo, counter_1_q, opcodedecoder_1_imm, registers_1_s,
       registers_1_t;
  wire [25:0] opcodedecoder_1_pseudo_address;
  wire [31:0] L1Cache_dout, undriven;
  wire [31:30] decoder_1_out30;

  Button button_1 (.out(button_1_out));
  and and_1 (and_1_out, ~HALT, clock_1_out);  // AND_Gate
  Clock clock_1 (.out(clock_1_out));
  Button button_2 (.out(button_2_out));
  // Shift_Register #(.length(3)) shift_register_1: pin names not known; wires that end beside it: button_1_out, and_1_out, and_1_out, shift_register_1_p4, shift_register_1_p5, shift_register_1_p6, shift_register_1_p7, shift_register_1_p5, shift_register_1_p6, shift_register_1_p7
  Counter #(.max('hffff), .width(16)) counter_1 (
    .clr(button_1_out), .load(button_2_out), .up(1'b1), .clk(shift_register_1_p5), .D(in_2), .carry(HALT),
    .Q(counter_1_q));  // open: count
  nor nor_1 (shift_register_1_p4, shift_register_1_p5, shift_register_1_p6);
  and and_2 (and_2_out, ~por_1_out, por_2_out);  // AND_Gate
  RAM #(.addrWidth(16), .clearpin("true"), .dataWidth(32), .\type ("nonvolatile")) L1Cache (
    .addr(counter_1_q), .we(WE), .oe(not_1_out), .clk(or_1_out), .din(undriven), .dout(L1Cache_dout));  // open: clr
  not not_1 (not_1_out, WE);
  or or_1 (or_1_out, shift_register_1_p5, and_2_out);
  POR #(.PorHighDuration(1)) por_1 (.out(por_1_out));
  POR por_2 (.out(por_2_out));
  // Probe on opcodedecoder_1_imm
  // Probe on multiplexer_1_out
  OpCodeDecoder opcodedecoder_1 (
    .instruction(L1Cache_dout), .operation(opcodedecoder_1_operation),
    .pseudo_address(opcodedecoder_1_pseudo_address), .rs(opcodedecoder_1_rs), .rt(opcodedecoder_1_rt),
    .IMM(opcodedecoder_1_imm), .shamt(opcodedecoder_1_shamt), .rd(opcodedecoder_1_rd),
    .I_Type(opcodedecoder_1_i_type), .J_Type(opcodedecoder_1_j_type), .RegEn(opcodedecoder_1_regen),
    .ALUEn(opcodedecoder_1_aluen));  // open: funct
  Multiplexer #(.enable("false"), .width(5)) multiplexer_1 (
    .in0(opcodedecoder_1_rd), .in1(opcodedecoder_1_rt), .out(multiplexer_1_out), .sel(opcodedecoder_1_i_type));
  // Probe on opcodedecoder_1_rs
  // Probe on opcodedecoder_1_rt
  Registers registers_1 (
    .data_in(alu_1_imm_out), .rd(multiplexer_1_out), .WE(opcodedecoder_1_regen), .clk(clk),
    .rs(opcodedecoder_1_rs), .rt(opcodedecoder_1_rt), .s(registers_1_s), .t(registers_1_t));
  // Probe on registers_1_s
  // Probe on registers_1_t
  ALU alu_1 (
    .IMM_TYPE(opcodedecoder_1_i_type), .rs_value(registers_1_s), .rt_value(registers_1_t),
    .IMM(opcodedecoder_1_imm), .SHAMT(opcodedecoder_1_shamt), .ALU_Enable(opcodedecoder_1_aluen),
    .alu_op(opcodedecoder_1_operation), .IMM_OUT(alu_1_imm_out), .Peek_LO(alu_1_peek_lo),
    .Peek_HI(alu_1_peek_hi));
  Decoder #(.select(5)) decoder_1 (
    .out0(add), .out1(sub), .out2(mult), .out3(multu), .out4(div), .out5(divu), .out6(and0), .out7(or0),
    .out8(nor0), .out9(xor0), .out10(lw), .out11(li), .out12(sw), .out13(sll0), .out14(srl0), .out15(sra0),
    .out16(slti), .out17(sltiu), .out18(beq), .out19(blez), .out20(bne), .out21(bgtz), .out22(j), .out23(jr),
    .out24(jal), .out25(jalr), .out26(mflo), .out27(mfhi), .out28(mtlo), .out29(mthi),
    .out30(decoder_1_out30[30]), .out31(decoder_1_out30[31]), .sel(opcodedecoder_1_operation),
    .en(opcodedecoder_1_aluen));
  // Probe on alu_1_imm_out
  // Probe on {alu_1_peek_hi, alu_1_peek_lo}
endmodule

module Registers (
  input  [15:0] data_in,
  input  [4:0] rd,
  input  WE,
  input  clk,
  input  [4:0] rs,
  input  [4:0] rt,
  output [15:0] s,
  output [15:0] t
);

  wire decoder_1_out0, decoder_1_out1, decoder_1_out2, decoder_1_out3, decoder_2_out0, decoder_2_out1,
       decoder_2_out2, decoder_2_out3, decoder_2_out4, decoder_2_out5, decoder_2_out6, decoder_2_out7,
       decoder_3_out0, decoder_3_out1, decoder_3_out2, decoder_3_out3, decoder_3_out4, decoder_3_out5,
       decoder_3_out6, decoder_3_out7, decoder_4_out0, decoder_4_out1, decoder_4_out2, decoder_4_out3,
       decoder_4_out4, decoder_4_out5, decoder_4_out6, decoder_4_out7, decoder_5_out0, decoder_5_out1,
       decoder_5_out2, decoder_5_out3, decoder_5_out4, decoder_5_out5, decoder_5_out6, decoder_5_out7;
  wire [15:0] a0, a1, a2, a3, at, fp, gp, k0, k1, r0, ra, s0, s1, s2, s3, s4, s5, s6, s7, sp, t0, t1, t2, t3,
       t4, t5, t6, t7, t8, t9, v0, v1;

  Decoder #(.select(2)) decoder_1 (
    .out0(decoder_1_out0), .out1(decoder_1_out1), .out2(decoder_1_out2), .out3(decoder_1_out3),
    .sel(rd[4:3]), .en(WE));
  Decoder #(.select(3)) decoder_2 (
    .out0(decoder_2_out0), .out1(decoder_2_out1), .out2(decoder_2_out2), .out3(decoder_2_out3),
    .out4(decoder_2_out4), .out5(decoder_2_out5), .out6(decoder_2_out6), .out7(decoder_2_out7),
    .sel(rd[2:0]), .en(decoder_1_out0));
  Register #(.width(16)) register_1 (.en(decoder_2_out0), .Q(r0), .clr(clk));  // open: D, clk
  Register #(.width(16)) u_at (.D(data_in), .en(decoder_2_out1), .clk(clk), .Q(at));  // open: clr
  Register #(.width(16)) u_v0 (.D(data_in), .en(decoder_2_out2), .clk(clk), .Q(v0));  // open: clr
  Register #(.width(16)) u_v1 (.D(data_in), .en(decoder_2_out3), .clk(clk), .Q(v1));  // open: clr
  Register #(.width(16)) u_a0 (.D(data_in), .en(decoder_2_out4), .clk(clk), .Q(a0));  // open: clr
  Register #(.width(16)) u_a1 (.D(data_in), .en(decoder_2_out5), .clk(clk), .Q(a1));  // open: clr
  Register #(.width(16)) u_a2 (.D(data_in), .en(decoder_2_out6), .clk(clk), .Q(a2));  // open: clr
  Register #(.width(16)) u_a3 (.D(data_in), .en(decoder_2_out7), .clk(clk), .Q(a3));  // open: clr
  Decoder #(.select(3)) decoder_3 (
    .out0(decoder_3_out0), .out1(decoder_3_out1), .out2(decoder_3_out2), .out3(decoder_3_out3),
    .out4(decoder_3_out4), .out5(decoder_3_out5), .out6(decoder_3_out6), .out7(decoder_3_out7),
    .sel(rd[2:0]), .en(decoder_1_out1));
  Register #(.width(16)) u_t0 (.D(data_in), .en(decoder_3_out0), .clk(clk), .Q(t0));  // open: clr
  Register #(.width(16)) u_t1 (.D(data_in), .en(decoder_3_out1), .clk(clk), .Q(t1));  // open: clr
  Register #(.width(16)) u_t2 (.D(data_in), .en(decoder_3_out2), .clk(clk), .Q(t2));  // open: clr
  Register #(.width(16)) u_t3 (.D(data_in), .en(decoder_3_out3), .clk(clk), .Q(t3));  // open: clr
  Register #(.width(16)) u_t4 (.D(data_in), .en(decoder_3_out4), .clk(clk), .Q(t4));  // open: clr
  Register #(.width(16)) u_t5 (.D(data_in), .en(decoder_3_out5), .clk(clk), .Q(t5));  // open: clr
  Register #(.width(16)) u_t6 (.D(data_in), .en(decoder_3_out6), .clk(clk), .Q(t6));  // open: clr
  Register #(.width(16)) u_t7 (.D(data_in), .en(decoder_3_out7), .clk(clk), .Q(t7));  // open: clr
  Decoder #(.select(3)) decoder_4 (
    .out0(decoder_4_out0), .out1(decoder_4_out1), .out2(decoder_4_out2), .out3(decoder_4_out3),
    .out4(decoder_4_out4), .out5(decoder_4_out5), .out6(decoder_4_out6), .out7(decoder_4_out7),
    .sel(rd[2:0]), .en(decoder_1_out2));
  Register #(.width(16)) u_s0 (.D(data_in), .en(decoder_4_out0), .clk(clk), .Q(s0));  // open: clr
  Register #(.width(16)) u_s1 (.D(data_in), .en(decoder_4_out1), .clk(clk), .Q(s1));  // open: clr
  Register #(.width(16)) u_s2 (.D(data_in), .en(decoder_4_out2), .clk(clk), .Q(s2));  // open: clr
  Register #(.width(16)) u_s3 (.D(data_in), .en(decoder_4_out3), .clk(clk), .Q(s3));  // open: clr
  Register #(.width(16)) u_s4 (.D(data_in), .en(decoder_4_out4), .clk(clk), .Q(s4));  // open: clr
  Register #(.width(16)) u_s5 (.D(data_in), .en(decoder_4_out5), .clk(clk), .Q(s5));  // open: clr
  Register #(.width(16)) u_s6 (.D(data_in), .en(decoder_4_out6), .clk(clk), .Q(s6));  // open: clr
  Register #(.width(16)) u_s7 (.D(data_in), .en(decoder_4_out7), .clk(clk), .Q(s7));  // open: clr
  Decoder #(.select(3)) decoder_5 (
    .out0(decoder_5_out0), .out1(decoder_5_out1), .out2(decoder_5_out2), .out3(decoder_5_out3),
    .out4(decoder_5_out4), .out5(decoder_5_out5), .out6(decoder_5_out6), .out7(decoder_5_out7),
    .sel(rd[2:0]), .en(decoder_1_out3));
  Register #(.width(16)) u_t8 (.D(data_in), .en(decoder_5_out0), .clk(clk), .Q(t8));  // open: clr
  Register #(.width(16)) u_t9 (.D(data_in), .en(decoder_5_out1), .clk(clk), .Q(t9));  // open: clr
  Register #(.width(16)) u_k0 (.D(data_in), .en(decoder_5_out2), .clk(clk), .Q(k0));  // open: clr
  Register #(.width(16)) u_k1 (.D(data_in), .en(decoder_5_out3), .clk(clk), .Q(k1));  // open: clr
  Register #(.width(16)) u_gp (.D(data_in), .en(decoder_5_out4), .clk(clk), .Q(gp));  // open: clr
  Register #(.width(16)) u_sp (.D(data_in), .en(decoder_5_out5), .clk(clk), .Q(sp));  // open: clr
  Register #(.width(16)) u_fp (.D(data_in), .en(decoder_5_out6), .clk(clk), .Q(fp));  // open: clr
  Register #(.width(16)) u_ra (.D(data_in), .en(decoder_5_out7), .clk(clk), .Q(ra));  // open: clr
  Multiplexer #(.enable("false"), .select(5), .width(16)) multiplexer_1 (
    .in0(r0), .in1(at), .in2(v0), .in3(v1), .in4(a0), .in5(a1), .in6(a2), .in7(a3), .in8(t0), .in9(t1),
    .in10(t2), .in11(t3), .in12(t4), .in13(t5), .in14(t6), .in15(t7), .in16(s0), .in17(s1), .in18(s2),
    .in19(s3), .in20(s4), .in21(s5), .in22(s6), .in23(s7), .in24(t8), .in25(t9), .in26(k0), .in27(k1),
    .in28(gp), .in29(sp), .in30(fp), .in31(ra), .out(s), .sel(rs));
  Multiplexer #(.enable("false"), .select(5), .width(16)) multiplexer_2 (
    .in0(r0), .in1(at), .in2(v0), .in3(v1), .in4(a0), .in5(a1), .in6(a2), .in7(a3), .in8(t0), .in9(t1),
    .in10(t2), .in11(t3), .in12(t4), .in13(t5), .in14(t6), .in15(t7), .in16(s0), .in17(s1), .in18(s2),
    .in19(s3), .in20(s4), .in21(s5), .in22(s6), .in23(s7), .in24(t8), .in25(t9), .in26(k0), .in27(k1),
    .in28(gp), .in29(sp), .in30(fp), .in31(ra), .out(t), .sel(rt));
endmodule

module ALU (
  input  IMM_TYPE,
  input  [15:0] rs_value,
  input  [15:0] rt_value,
  input  [15:0] IMM,
  input  [4:0] SHAMT,
  input  ALU_Enable,
  input  [4:0] alu_op,
  output [15:0] IMM_OUT,
  output [15:0] Peek_LO,
  output [15:0] Peek_HI
);

  wire add, and0, beq, bgtz, blez, bne, clock_1_out, div, divu, j, jal, jalr, jr, li, lw, mfhi, mflo, mthi,
       mtlo, mult, multu, nor0, or0, or_2_out, or_3_out, por_1_out, sll0, slti, sltiu, sra0, srl0, sub, sw,
       xor0;
  wire [3:0] multiplexer_5_out, multiplexer_6_out, multiplexer_7_out;
  wire [15:0] adder_1_out, and_1_out, controlled_buffer_3_out, controlled_buffer_4_out, divider_1_out,
       divider_1_rem, divider_2_out, divider_2_rem, multiplexer_1_out, multiplexer_2_out, multiplexer_3_out,
       multiplexer_4_out, multiplier_1_cout, multiplier_1_out, multiplier_2_cout, multiplier_2_out,
       nor_1_out, or_1_out, shifter_1_out, shifter_2_out, shifter_3_out, subtractor_1_out, xor_1_out;
  wire [31:30] decoder_1_out30;

  Multiplexer #(.enable("false"), .width(16)) multiplexer_1 (
    .in0(rt_value), .in1(IMM), .out(multiplexer_1_out), .sel(IMM_TYPE));
  Multiplexer #(.enable("false"), .width(16)) multiplexer_2 (
    .in0(rt_value), .in1(IMM), .out(multiplexer_2_out), .sel(IMM_TYPE));
  Multiplexer #(.enable("false"), .width(16)) multiplexer_3 (
    .in0(rt_value), .in1(IMM), .out(multiplexer_3_out), .sel(IMM_TYPE));
  Multiplexer #(.enable("false"), .width(16)) multiplexer_4 (
    .in0(rt_value), .in1(IMM), .out(multiplexer_4_out), .sel(IMM_TYPE));
  Multiplexer #(.enable("false"), .width(4)) multiplexer_5 (
    .in0(rs_value[3:0]), .in1(SHAMT[3:0]), .out(multiplexer_5_out), .sel(IMM_TYPE));
  Multiplexer #(.enable("false"), .width(4)) multiplexer_6 (
    .in0(rs_value[3:0]), .in1(SHAMT[3:0]), .out(multiplexer_6_out), .sel(IMM_TYPE));
  Multiplexer #(.enable("false"), .width(4)) multiplexer_7 (
    .in0(rs_value[3:0]), .in1(SHAMT[3:0]), .out(multiplexer_7_out), .sel(IMM_TYPE));
  assign IMM_OUT = add ? adder_1_out : 16'bz;  // Controlled_Buffer controlled_buffer_1
  Adder #(.width(16)) adder_1 (.a(rs_value), .b(multiplexer_1_out), .out(adder_1_out));  // open: cin, cout
  assign IMM_OUT = sub ? subtractor_1_out : 16'bz;  // Controlled_Buffer controlled_buffer_2
  Subtractor #(.width(16)) subtractor_1 (.a(rs_value), .b(rt_value), .out(subtractor_1_out));  // open: bin, bout
  assign controlled_buffer_3_out = mult ? multiplier_1_out : 16'bz;  // Controlled_Buffer controlled_buffer_3
  Multiplier #(.mode("twosComplement"), .width(16)) multiplier_1 (
    .a(rs_value), .b(rt_value), .out(multiplier_1_out), .cout(multiplier_1_cout));  // open: cin
  assign controlled_buffer_4_out = mult ? multiplier_1_cout : 16'bz;  // Controlled_Buffer controlled_buffer_4
  assign controlled_buffer_3_out = multu ? multiplier_2_out : 16'bz;  // Controlled_Buffer controlled_buffer_5
  Multiplier #(.width(16)) multiplier_2 (
    .a(rs_value), .b(rt_value), .out(multiplier_2_out), .cout(multiplier_2_cout));  // open: cin
  assign controlled_buffer_4_out = multu ? multiplier_2_cout : 16'bz;  // Controlled_Buffer controlled_buffer_6
  assign controlled_buffer_3_out = div ? divider_1_out : 16'bz;  // Controlled_Buffer controlled_buffer_7
  Divider #(.mode("twosComplement"), .width(16)) divider_1 (
    .a(rs_value), .b(rt_value), .out(divider_1_out), .rem(divider_1_rem));  // open: upper
  assign controlled_buffer_4_out = div ? divider_1_rem : 16'bz;  // Controlled_Buffer controlled_buffer_8
  assign controlled_buffer_3_out = divu ? divider_2_out : 16'bz;  // Controlled_Buffer controlled_buffer_9
  Divider #(.width(16)) divider_2 (
    .a(rs_value), .b(rt_value), .out(divider_2_out), .rem(divider_2_rem));  // open: upper
  assign controlled_buffer_4_out = divu ? divider_2_rem : 16'bz;  // Controlled_Buffer controlled_buffer_10
  assign controlled_buffer_3_out = mtlo ? rs_value : 16'bz;  // Controlled_Buffer controlled_buffer_11
  assign controlled_buffer_4_out = mthi ? rs_value : 16'bz;  // Controlled_Buffer controlled_buffer_12
  assign and_1_out = rs_value & multiplexer_2_out;  // AND_Gate and_1, 16 bits wide
  assign IMM_OUT = and0 ? and_1_out : 16'bz;  // Controlled_Buffer controlled_buffer_13
  assign or_1_out = rs_value | multiplexer_3_out;  // OR_Gate or_1, 16 bits wide
  assign IMM_OUT = or0 ? or_1_out : 16'bz;  // Controlled_Buffer controlled_buffer_14
  assign nor_1_out = ~(rs_value | rt_value);  // NOR_Gate nor_1, 16 bits wide
  assign IMM_OUT = nor0 ? nor_1_out : 16'bz;  // Controlled_Buffer controlled_buffer_15
  assign xor_1_out = rs_value ^ multiplexer_4_out;  // XOR_Gate xor_1, 16 bits wide
  assign IMM_OUT = xor0 ? xor_1_out : 16'bz;  // Controlled_Buffer controlled_buffer_16
  assign IMM_OUT = sll0 ? shifter_1_out : 16'bz;  // Controlled_Buffer controlled_buffer_17
  Shifter #(.width(16)) shifter_1 (.in(rt_value), .\dist (multiplexer_5_out), .out(shifter_1_out));
  assign IMM_OUT = srl0 ? shifter_2_out : 16'bz;  // Controlled_Buffer controlled_buffer_18
  Shifter #(.shift("lr"), .width(16)) shifter_2 (.in(rt_value), .\dist (multiplexer_6_out), .out(shifter_2_out));
  assign IMM_OUT = sra0 ? shifter_3_out : 16'bz;  // Controlled_Buffer controlled_buffer_19
  Shifter #(.shift("ar"), .width(16)) shifter_3 (.in(rt_value), .\dist (multiplexer_7_out), .out(shifter_3_out));
  assign IMM_OUT = li ? IMM : 16'bz;  // Controlled_Buffer controlled_buffer_20
  Register #(.width(16)) LO (
    .D(controlled_buffer_3_out), .en(or_2_out), .clk(clock_1_out), .Q(Peek_LO), .clr(por_1_out));
  or or_2 (or_2_out, mult, multu);
  Register #(.width(16)) HI (
    .D(controlled_buffer_4_out), .en(or_3_out), .clk(clock_1_out), .Q(Peek_HI), .clr(por_1_out));
  or or_3 (or_3_out, mult, multu);
  Clock clock_1 (.out(clock_1_out));
  assign IMM_OUT = mflo ? Peek_LO : 16'bz;  // Controlled_Buffer controlled_buffer_21
  assign IMM_OUT = mfhi ? Peek_HI : 16'bz;  // Controlled_Buffer controlled_buffer_22
  POR por_1 (.out(por_1_out));
  Decoder #(.select(5)) decoder_1 (
    .out0(add), .out1(sub), .out2(mult), .out3(multu), .out4(div), .out5(divu), .out6(and0), .out7(or0),
    .out8(nor0), .out9(xor0), .out10(lw), .out11(li), .out12(sw), .out13(sll0), .out14(srl0), .out15(sra0),
    .out16(slti), .out17(sltiu), .out18(beq), .out19(blez), .out20(bne), .out21(bgtz), .out22(j), .out23(jr),
    .out24(jal), .out25(jalr), .out26(mflo), .out27(mfhi), .out28(mtlo), .out29(mthi),
    .out30(decoder_1_out30[30]), .out31(decoder_1_out30[31]), .sel(alu_op), .en(ALU_Enable));
endmodule

module OpCodeDecoder (
  input  [31:0] instruction,
  output [4:0] operation,
  output [25:0] pseudo_address,
  output [4:0] rs,
  output [4:0] rt,
  output [15:0] IMM,
  output [5:0] funct,
  output [4:0] shamt,
  output [4:0] rd,
  output I_Type,
  output J_Type,
  output RegEn,
  output ALUEn
);

  wire add, and0, beq, bgtz, bitfinder_1_found, bitfinder_2_found, bitfinder_3_found, bitfinder_4_found,
       bitfinder_5_found, bitfinder_6_found, bitfinder_7_found, bitfinder_8_found, bitfinder_9_found,
       bitfinder_10_found, bitfinder_11_found, bitfinder_12_found, bitfinder_13_found, bitfinder_14_found,
       bitfinder_15_found, bitfinder_16_found, bitfinder_17_found, bitfinder_18_found, bitfinder_19_found,
       bitfinder_20_found, bitfinder_21_found, bitfinder_22_found, bitfinder_23_found, bitfinder_24_found,
       bitfinder_25_found, bitfinder_26_found, bitfinder_27_found, bitfinder_28_found, bitfinder_29_found,
       bitfinder_30_found, bitfinder_31_found, bitfinder_32_found, bitfinder_33_found, bitfinder_34_found,
       bitfinder_35_found, bitfinder_36_found, bitfinder_37_found, blez, bne, div, divu, j_t, jal, jalr, jr,
       li, lw, mfhi, mflo, mthi, mtlo, mult, multu, nor0, or0, R, sll0, slti, sltiu, sra0, srl0, sub, sw,
       xor0;
  wire [5:0] xor_1_out, xor_2_out, xor_3_out, xor_4_out, xor_5_out, xor_6_out, xor_7_out, xor_8_out,
       xor_9_out, xor_10_out, xor_11_out, xor_12_out, xor_13_out, xor_14_out, xor_15_out, xor_16_out,
       xor_17_out, xor_18_out, xor_19_out, xor_20_out, xor_21_out, xor_22_out, xor_23_out, xor_24_out,
       xor_25_out, xor_26_out, xor_27_out, xor_28_out, xor_29_out, xor_30_out, xor_31_out, xor_32_out,
       xor_33_out;
  wire [10:10] pull_resistor_1_node;
  wire [18:18] pull_resistor_2_node;
  wire [31:30] undriven;

  assign add = I_Type ? ~bitfinder_1_found : 1'bz;  // Controlled_Inverter controlled_inverter_1
  assign xor_1_out = instruction[31:26] ^ 6'b001000;  // XOR_Gate xor_1, 6 bits wide
  BitFinder #(.width(6)) bitfinder_1 (.in(xor_1_out), .found(bitfinder_1_found));  // open: index
  assign and0 = I_Type ? ~bitfinder_2_found : 1'bz;  // Controlled_Inverter controlled_inverter_2
  assign xor_2_out = instruction[31:26] ^ 6'b001100;  // XOR_Gate xor_2, 6 bits wide
  BitFinder #(.width(6)) bitfinder_2 (.in(xor_2_out), .found(bitfinder_2_found));  // open: index
  assign or0 = I_Type ? ~bitfinder_3_found : 1'bz;  // Controlled_Inverter controlled_inverter_3
  assign xor_3_out = instruction[31:26] ^ 6'b001101;  // XOR_Gate xor_3, 6 bits wide
  BitFinder #(.width(6)) bitfinder_3 (.in(xor_3_out), .found(bitfinder_3_found));  // open: index
  assign beq = I_Type ? ~bitfinder_4_found : 1'bz;  // Controlled_Inverter controlled_inverter_4
  assign xor_4_out = instruction[31:26] ^ 6'b000100;  // XOR_Gate xor_4, 6 bits wide
  BitFinder #(.width(6)) bitfinder_4 (.in(xor_4_out), .found(bitfinder_4_found));  // open: index
  assign blez = I_Type ? ~bitfinder_5_found : 1'bz;  // Controlled_Inverter controlled_inverter_5
  assign xor_5_out = instruction[31:26] ^ 6'b000110;  // XOR_Gate xor_5, 6 bits wide
  BitFinder #(.width(6)) bitfinder_5 (.in(xor_5_out), .found(bitfinder_5_found));  // open: index
  assign bne = I_Type ? ~bitfinder_6_found : 1'bz;  // Controlled_Inverter controlled_inverter_6
  assign xor_6_out = instruction[31:26] ^ 6'b000101;  // XOR_Gate xor_6, 6 bits wide
  BitFinder #(.width(6)) bitfinder_6 (.in(xor_6_out), .found(bitfinder_6_found));  // open: index
  assign bgtz = I_Type ? ~bitfinder_7_found : 1'bz;  // Controlled_Inverter controlled_inverter_7
  assign xor_7_out = instruction[31:26] ^ 6'b000111;  // XOR_Gate xor_7, 6 bits wide
  BitFinder #(.width(6)) bitfinder_7 (.in(xor_7_out), .found(bitfinder_7_found));  // open: index
  assign lw = I_Type ? ~bitfinder_8_found : 1'bz;  // Controlled_Inverter controlled_inverter_8
  assign xor_8_out = instruction[31:26] ^ 6'b100011;  // XOR_Gate xor_8, 6 bits wide
  BitFinder #(.width(6)) bitfinder_8 (.in(xor_8_out), .found(bitfinder_8_found));  // open: index
  assign sw = I_Type ? ~bitfinder_9_found : 1'bz;  // Controlled_Inverter controlled_inverter_9
  assign xor_9_out = instruction[31:26] ^ 6'b101011;  // XOR_Gate xor_9, 6 bits wide
  BitFinder #(.width(6)) bitfinder_9 (.in(xor_9_out), .found(bitfinder_9_found));  // open: index
  assign slti = I_Type ? ~bitfinder_10_found : 1'bz;  // Controlled_Inverter controlled_inverter_10
  assign xor_10_out = instruction[31:26] ^ 6'b001010;  // XOR_Gate xor_10, 6 bits wide
  BitFinder #(.width(6)) bitfinder_10 (.in(xor_10_out), .found(bitfinder_10_found));  // open: index
  assign sltiu = I_Type ? ~bitfinder_11_found : 1'bz;  // Controlled_Inverter controlled_inverter_11
  assign xor_11_out = instruction[31:26] ^ 6'b001011;  // XOR_Gate xor_11, 6 bits wide
  BitFinder #(.width(6)) bitfinder_11 (.in(xor_11_out), .found(bitfinder_11_found));  // open: index
  assign li = I_Type ? ~bitfinder_12_found : 1'bz;  // Controlled_Inverter controlled_inverter_12
  assign xor_12_out = instruction[31:26] ^ 6'b001111;  // XOR_Gate xor_12, 6 bits wide
  BitFinder #(.width(6)) bitfinder_12 (.in(xor_12_out), .found(bitfinder_12_found));  // open: index
  Pull_Resistor pull_resistor_1 (.node(pull_resistor_1_node[10]));
  assign RegEn = I_Type ? bitfinder_13_found : 1'bz;  // Controlled_Buffer controlled_buffer_1
  BitFinder #(.width(12)) bitfinder_13 (
    .in({li, sltiu, slti, sw, lw, {4{pull_resistor_1_node[10]}}, or0, and0, add}), .found(bitfinder_13_found));  // open: index
  assign ALUEn = I_Type ? bitfinder_14_found : 1'bz;  // Controlled_Buffer controlled_buffer_2
  BitFinder #(.width(12)) bitfinder_14 (
    .in({li, {8{pull_resistor_1_node[10]}}, or0, and0, add}), .found(bitfinder_14_found));  // open: index
  and and_1 (R, ~instruction[26], ~instruction[27], ~instruction[28], ~instruction[29], ~instruction[31]);  // AND_Gate
  and and_2 (J_Type, ~instruction[28], instruction[27], ~instruction[29], ~instruction[30], ~instruction[31]);  // AND_Gate
  nor nor_1 (I_Type, R, J_Type);
  assign xor_13_out = instruction[31:26] ^ 6'b000010;  // XOR_Gate xor_13, 6 bits wide
  assign xor_14_out = instruction[31:26] ^ 6'b000011;  // XOR_Gate xor_14, 6 bits wide
  assign j_t = J_Type ? ~bitfinder_15_found : 1'bz;  // Controlled_Inverter controlled_inverter_13
  BitFinder #(.width(6)) bitfinder_15 (.in(xor_13_out), .found(bitfinder_15_found));  // open: index
  assign jal = J_Type ? ~bitfinder_16_found : 1'bz;  // Controlled_Inverter controlled_inverter_14
  BitFinder #(.width(6)) bitfinder_16 (.in(xor_14_out), .found(bitfinder_16_found));  // open: index
  assign RegEn = J_Type ? jal : 1'bz;  // Controlled_Buffer controlled_buffer_3
  assign ALUEn = J_Type ? 1'b0 : 1'bz;  // Controlled_Buffer controlled_buffer_4
  assign xor_15_out = instruction[5:0] ^ 6'b100000;  // XOR_Gate xor_15, 6 bits wide
  assign xor_16_out = instruction[5:0] ^ 6'b100010;  // XOR_Gate xor_16, 6 bits wide
  assign xor_17_out = instruction[5:0] ^ 6'b011000;  // XOR_Gate xor_17, 6 bits wide
  assign xor_18_out = instruction[5:0] ^ 6'b011001;  // XOR_Gate xor_18, 6 bits wide
  assign xor_19_out = instruction[5:0] ^ 6'b011010;  // XOR_Gate xor_19, 6 bits wide
  assign xor_20_out = instruction[5:0] ^ 6'b011011;  // XOR_Gate xor_20, 6 bits wide
  assign xor_21_out = instruction[5:0] ^ 6'b010000;  // XOR_Gate xor_21, 6 bits wide
  assign xor_22_out = instruction[5:0] ^ 6'b010010;  // XOR_Gate xor_22, 6 bits wide
  assign xor_23_out = instruction[5:0] ^ 6'b100100;  // XOR_Gate xor_23, 6 bits wide
  assign xor_24_out = instruction[5:0] ^ 6'b100101;  // XOR_Gate xor_24, 6 bits wide
  assign xor_25_out = instruction[5:0] ^ 6'b100111;  // XOR_Gate xor_25, 6 bits wide
  assign xor_26_out = instruction[5:0] ^ 6'b100110;  // XOR_Gate xor_26, 6 bits wide
  assign xor_27_out = instruction[5:0] ^ {6{1'b0}};  // XOR_Gate xor_27, 6 bits wide
  assign xor_28_out = instruction[5:0] ^ 6'b000010;  // XOR_Gate xor_28, 6 bits wide
  assign xor_29_out = instruction[5:0] ^ 6'b000011;  // XOR_Gate xor_29, 6 bits wide
  assign xor_30_out = instruction[5:0] ^ 6'b010011;  // XOR_Gate xor_30, 6 bits wide
  assign xor_31_out = instruction[5:0] ^ 6'b010001;  // XOR_Gate xor_31, 6 bits wide
  assign xor_32_out = instruction[5:0] ^ 6'b001001;  // XOR_Gate xor_32, 6 bits wide
  assign xor_33_out = instruction[5:0] ^ 6'b001000;  // XOR_Gate xor_33, 6 bits wide
  Pull_Resistor pull_resistor_2 (.node(pull_resistor_2_node[18]));
  assign add = R ? ~bitfinder_17_found : 1'bz;  // Controlled_Inverter controlled_inverter_15
  BitFinder #(.width(6)) bitfinder_17 (.in(xor_15_out), .found(bitfinder_17_found));  // open: index
  assign sub = R ? ~bitfinder_18_found : 1'bz;  // Controlled_Inverter controlled_inverter_16
  BitFinder #(.width(6)) bitfinder_18 (.in(xor_16_out), .found(bitfinder_18_found));  // open: index
  assign mult = R ? ~bitfinder_19_found : 1'bz;  // Controlled_Inverter controlled_inverter_17
  BitFinder #(.width(6)) bitfinder_19 (.in(xor_17_out), .found(bitfinder_19_found));  // open: index
  assign multu = R ? ~bitfinder_20_found : 1'bz;  // Controlled_Inverter controlled_inverter_18
  BitFinder #(.width(6)) bitfinder_20 (.in(xor_18_out), .found(bitfinder_20_found));  // open: index
  assign div = R ? ~bitfinder_21_found : 1'bz;  // Controlled_Inverter controlled_inverter_19
  BitFinder #(.width(6)) bitfinder_21 (.in(xor_19_out), .found(bitfinder_21_found));  // open: index
  assign divu = R ? ~bitfinder_22_found : 1'bz;  // Controlled_Inverter controlled_inverter_20
  BitFinder #(.width(6)) bitfinder_22 (.in(xor_20_out), .found(bitfinder_22_found));  // open: index
  assign mfhi = R ? ~bitfinder_23_found : 1'bz;  // Controlled_Inverter controlled_inverter_21
  BitFinder #(.width(6)) bitfinder_23 (.in(xor_21_out), .found(bitfinder_23_found));  // open: index
  assign mflo = R ? ~bitfinder_24_found : 1'bz;  // Controlled_Inverter controlled_inverter_22
  BitFinder #(.width(6)) bitfinder_24 (.in(xor_22_out), .found(bitfinder_24_found));  // open: index
  assign and0 = R ? ~bitfinder_25_found : 1'bz;  // Controlled_Inverter controlled_inverter_23
  BitFinder #(.width(6)) bitfinder_25 (.in(xor_23_out), .found(bitfinder_25_found));  // open: index
  assign or0 = R ? ~bitfinder_26_found : 1'bz;  // Controlled_Inverter controlled_inverter_24
  BitFinder #(.width(6)) bitfinder_26 (.in(xor_24_out), .found(bitfinder_26_found));  // open: index
  assign nor0 = R ? ~bitfinder_27_found : 1'bz;  // Controlled_Inverter controlled_inverter_25
  BitFinder #(.width(6)) bitfinder_27 (.in(xor_25_out), .found(bitfinder_27_found));  // open: index
  assign xor0 = R ? ~bitfinder_28_found : 1'bz;  // Controlled_Inverter controlled_inverter_26
  BitFinder #(.width(6)) bitfinder_28 (.in(xor_26_out), .found(bitfinder_28_found));  // open: index
  assign sll0 = R ? ~bitfinder_29_found : 1'bz;  // Controlled_Inverter controlled_inverter_27
  BitFinder #(.width(6)) bitfinder_29 (.in(xor_27_out), .found(bitfinder_29_found));  // open: index
  assign srl0 = R ? ~bitfinder_30_found : 1'bz;  // Controlled_Inverter controlled_inverter_28
  BitFinder #(.width(6)) bitfinder_30 (.in(xor_28_out), .found(bitfinder_30_found));  // open: index
  assign sra0 = R ? ~bitfinder_31_found : 1'bz;  // Controlled_Inverter controlled_inverter_29
  BitFinder #(.width(6)) bitfinder_31 (.in(xor_29_out), .found(bitfinder_31_found));  // open: index
  assign mtlo = R ? ~bitfinder_32_found : 1'bz;  // Controlled_Inverter controlled_inverter_30
  BitFinder #(.width(6)) bitfinder_32 (.in(xor_30_out), .found(bitfinder_32_found));  // open: index
  assign mthi = R ? ~bitfinder_33_found : 1'bz;  // Controlled_Inverter controlled_inverter_31
  BitFinder #(.width(6)) bitfinder_33 (.in(xor_31_out), .found(bitfinder_33_found));  // open: index
  assign jalr = R ? ~bitfinder_34_found : 1'bz;  // Controlled_Inverter controlled_inverter_32
  BitFinder #(.width(6)) bitfinder_34 (.in(xor_32_out), .found(bitfinder_34_found));  // open: index
  assign jr = R ? ~bitfinder_35_found : 1'bz;  // Controlled_Inverter controlled_inverter_33
  BitFinder #(.width(6)) bitfinder_35 (.in(xor_33_out), .found(bitfinder_35_found));  // open: index
  BitFinder #(.width(19)) bitfinder_36 (
    .in({jr, jalr, mthi, mtlo, sra0, srl0, sll0, xor0, nor0, or0, and0, mflo, mfhi, divu, div, multu, mult, sub, add}),
    .found(bitfinder_36_found));  // open: index
  BitFinder #(.width(19)) bitfinder_37 (
    .in({{2{pull_resistor_2_node[18]}}, mthi, mtlo, sra0, srl0, sll0, xor0, nor0, or0, and0, mflo, mfhi, divu, div, multu, mult, sub, add}),
    .found(bitfinder_37_found));  // open: index
  BitFinder #(.width(32)) bitfinder_38 (
    .in({undriven, mthi, mtlo, mfhi, mflo, jalr, jal, jr, j_t, bgtz, bne, blez, beq, sltiu, slti, sra0, srl0, sll0, sw, li, lw, xor0, nor0, or0, and0, divu, div, multu, mult, sub, add}),
    .index(operation));  // open: found
  Pull_Resistor pull_resistor_3 (.node(add));
  Pull_Resistor pull_resistor_4 (.node(sub));
  Pull_Resistor pull_resistor_5 (.node(mult));
  Pull_Resistor pull_resistor_6 (.node(multu));
  Pull_Resistor pull_resistor_7 (.node(div));
  Pull_Resistor pull_resistor_8 (.node(divu));
  Pull_Resistor pull_resistor_9 (.node(and0));
  Pull_Resistor pull_resistor_10 (.node(or0));
  Pull_Resistor pull_resistor_11 (.node(nor0));
  Pull_Resistor pull_resistor_12 (.node(xor0));
  Pull_Resistor pull_resistor_13 (.node(lw));
  Pull_Resistor pull_resistor_14 (.node(li));
  Pull_Resistor pull_resistor_15 (.node(sw));
  Pull_Resistor pull_resistor_16 (.node(sll0));
  Pull_Resistor pull_resistor_17 (.node(srl0));
  Pull_Resistor pull_resistor_18 (.node(sra0));
  Pull_Resistor pull_resistor_19 (.node(slti));
  Pull_Resistor pull_resistor_20 (.node(sltiu));
  Pull_Resistor pull_resistor_21 (.node(beq));
  Pull_Resistor pull_resistor_22 (.node(blez));
  Pull_Resistor pull_resistor_23 (.node(bne));
  Pull_Resistor pull_resistor_24 (.node(bgtz));
  Pull_Resistor pull_resistor_25 (.node(j_t));
  Pull_Resistor pull_resistor_26 (.node(jr));
  Pull_Resistor pull_resistor_27 (.node(jal));
  Pull_Resistor pull_resistor_28 (.node(jalr));
  Pull_Resistor pull_resistor_29 (.node(mflo));
  Pull_Resistor pull_resistor_30 (.node(mfhi));
  Pull_Resistor pull_resistor_31 (.node(mtlo));
  Pull_Resistor pull_resistor_32 (.node(mthi));
  assign RegEn = R ? bitfinder_36_found : 1'bz;  // Controlled_Buffer controlled_buffer_5
  assign ALUEn = R ? bitfinder_37_found : 1'bz;  // Controlled_Buffer controlled_buffer_6

  assign funct = instruction[5:0];
  assign IMM = instruction[15:0];
  assign pseudo_address = instruction[25:0];
  assign rd = instruction[15:11];
  assign rs = instruction[25:21];
  assign rt = instruction[20:16];
  assign shamt = instruction[10:6];

  // Other names for the same wires on the sheet: ALU_Enable = ALUEn; I = I_Type; opcode[5:0] = instruction[31:26];
  //   J = J_Type; Register_Enable = RegEn
endmodule
